# Fritzing sketch khamosh roshan (saved by Fritzing 0.9.4)
breadboards: 1

parts:
  LED1 = LED - 5mm [color="Green (555nm)" package="5 mm [THT]"]
  Part1 = Arduino Uno (Rev3)
  R1 = Resistor [tolerance=±5% resistance=220 package=THT]
  LED2 = LED - 5mm [color="Red (633nm)" package="5 mm [THT]"]
  R2 = Resistor [tolerance=±5% resistance=220 package=THT]

nets:
  N1: LED1.cathode, Part1.D13/SCK
  N2: LED1.anode, R1.Pin_1
  N3: Part1.D10_PWM/SS, LED2.cathode
  N4: Part1.GND, R1.Pin_0
  N5: Part1.VIN, LED2.anode, R2.Pin_1

// code stored in the sketch: Untitled.ino
 conat int ledpin=12;
     
        void setup(){

   pinMode(ledpin,OUTPUT);

    Serail.begin(9600);
}
      void loop(){

    if(Serial.available()>0){

  string value=Serial.readStringUntil('\n');

   if(value=="ON"||value=="on"||value=="H"||value=="h"){
 
  digitalWrite(ledpin,HiGH);

}
else if(value=="OFF"||value=="off"||value=="L"||value=="l"){
 
 digitalWrite(ledpin,LOW);

};
};
}
