# Fritzing sketch Untitled Sketch1 (saved by Fritzing 0.9.4)
breadboards: 1

parts:
  U1 = POT [package=pot_mammoth]
  Part1 = Arduino Uno (Rev3)
  LCD1 = LCD screen
  hc-sr1 = hc-sr04

nets:
  5V: U1.S, Part1.5V, LCD1.VDD, LCD1.LED+, hc-sr1.VCC
  N1: U1.A, LCD1.V0
  GND: U1.E, Part1.D10_PWM/SS, Part1.GND, LCD1.VSS, LCD1.R/W, LCD1.LED-, hc-sr1.Trig, hc-sr1.GND
  N2: Part1.D9_PWM, hc-sr1.Echo
  N3: Part1.D11_PWM/MOSI, LCD1.E
  N4: Part1.D12/MISO, LCD1.RS
  N5: Part1.D4, LCD1.DB7
  N6: Part1.D5_PWM, LCD1.DB6
  N7: Part1.D6_PWM, LCD1.DB5
  N8: Part1.D7, LCD1.DB4
