# Fritzing sketch Untitled Sketch11 (saved by Fritzing 0.9.4)
breadboards: 1

parts:
  Part1 = Arduino Uno (Rev3)
  hc-sr1 = hc-sr04
  LED1 = LED - 5mm [color="Red (633nm)" package="5 mm [THT]"]
  R1 = Resistor [tolerance=±5% resistance=220 package=THT]

nets:
  N1: Part1.D9_PWM, hc-sr1.Echo
  N2: Part1.D10_PWM/SS, hc-sr1.Trig
  N3: Part1.D11_PWM/MOSI, LED1.anode
  GND: Part1.GND, hc-sr1.GND, R1.Pin_0
  5V: Part1.5V, hc-sr1.VCC
  N4: LED1.cathode, R1.Pin_1
